// Logisim project CPU.circ as structural Verilog
module CPU (
  input  [1:0] in_1,
  output [7:0] Entrada_1,
  output [15:0] \Saída_1 
);

  wire and_1_out, Clock, K0, K1, K2, K3, L8, L9, S0, S1, S2, S3, S4, S5, S6, S7, S8;
  wire [3:0] HEX0, HEX1, ula4_1_rgto;

  LED u_L9 (.in(L9));
  // DipSwitch #(.NSwitches(1)) S9: pin names not known; wires that end beside it: Clock
  Hex_Digit_Display hex_digit_display_1 (.value(\Saída_1 [11:8]));  // open: dp
  Hex_Digit_Display hex_digit_display_2 (.value(\Saída_1 [15:12]));  // open: dp
  LED L7 (.in(Entrada_1[7]));
  LED u_L8 (.in(L8));
  // DipSwitch #(.NSwitches(1)) S6: pin names not known; wires that end beside it: S6
  // DipSwitch #(.NSwitches(1)) S7: pin names not known; wires that end beside it: S7
  // DipSwitch #(.NSwitches(1)) S8: pin names not known; wires that end beside it: S8
  // Digital_Oscilloscope #(.nState(20)) digital_oscilloscope_1: pin names not known; wires that end beside it: Clock, Entrada_1[0], Entrada_1[1], Entrada_1[2], Entrada_1[3], Entrada_1[4], Entrada_1[5], Entrada_1[5], Entrada_1[7], S0
  Hex_Digit_Display hex_digit_display_3 (.value(\Saída_1 [3:0]));  // open: dp
  Hex_Digit_Display hex_digit_display_4 (.value(\Saída_1 [7:4]));  // open: dp
  LED L5 (.in(Entrada_1[5]));
  LED L6 (.in(Entrada_1[6]));
  LED L4 (.in(Entrada_1[4]));
  // DipSwitch #(.NSwitches(1)) S4: pin names not known; wires that end beside it: S4
  // DipSwitch #(.NSwitches(1)) S5: pin names not known; wires that end beside it: S5
  Count8 count8_1 (.Clear(S0), .Jump(and_1_out), .Clock(Clock), .Addr(\Saída_1 [3:0]), .Cont(Entrada_1));
  and and_1 (and_1_out, \Saída_1 [10], \Saída_1 [11], Clock);
  Hex_Digit_Display hex_digit_display_5 (.value(HEX1));  // open: dp
  LED L2 (.in(Entrada_1[2]));
  LED L1 (.in(Entrada_1[1]));
  LED L3 (.in(Entrada_1[3]));
  // DipSwitch #(.NSwitches(1)) S3: pin names not known; wires that end beside it: S3
  // DipSwitch #(.NSwitches(1)) S2: pin names not known; wires that end beside it: S2
  // DipSwitch #(.NSwitches(1)) S1: pin names not known; wires that end beside it: S1
  ROM_256x16_2 rom_256x16_2_1 (.busAddr8(Entrada_1), .busData16(\Saída_1 ), .CLK(Clock));
  Hex_Digit_Display hex_digit_display_6 (.value(HEX0));  // open: dp
  LED L0 (.in(Entrada_1[0]));
  // DipSwitch #(.NSwitches(1)) S0: pin names not known; wires that end beside it: S0
  Button u_K3 (.out(K3));
  Button u_K2 (.out(K2));
  Button u_K1 (.out(K1));
  Button u_K0 (.out(K0));
  Reg4 reg4_1 (.Clock(Clock), .Load(1'b1), .Q(HEX1), .D(4'b0101), .Clear(S0));
  ULA4 ula4_1 (.RgIN(HEX1), .Operando(4'b0100), .RgTO(ula4_1_rgto), .ULA(in_1));
  Reg4 reg4_2 (.Clock(Clock), .Load(1'b1), .Q(HEX0), .D(ula4_1_rgto), .Clear(S0));

  // Other names for the same wires on the sheet: Entrada[7:0] = Entrada_1; L0 = Entrada_1[0]; L1 = Entrada_1[1];
  //   L2 = Entrada_1[2]; L3 = Entrada_1[3]; L4 = Entrada_1[4]; L5 = Entrada_1[5]; L6 = Entrada_1[6];
  //   L7 = Entrada_1[7]; S9 = Clock; HEX2[3:0] = \Saída_1 [3:0]; Operando[3:0] = \Saída_1 [3:0];
  //   Saida[15:0] = \Saída_1 ; Disponivel[3:0] = \Saída_1 [7:4]; HEX3[3:0] = \Saída_1 [7:4];
  //   HEX4[3:0] = \Saída_1 [11:8]; ULA[1:0] = \Saída_1 [9:8]; JMP[1:0] = \Saída_1 [11:10];
  //   HEX5[3:0] = \Saída_1 [15:12]; RgIN[1:0] = \Saída_1 [13:12]; RgTO[1:0] = \Saída_1 [15:14]
endmodule

module ULA4 (
  input  [3:0] RgIN,
  input  [3:0] Operando,
  input  [1:0] ULA,
  output [3:0] RgTO
);

  wire [3:0] adder_1_out, divider_1_out, multiplier_1_out, subtractor_1_out;

  Adder #(.width(4)) adder_1 (.a(RgIN), .b(Operando), .out(adder_1_out));  // open: cin, cout
  Multiplier #(.width(4)) multiplier_1 (.a(Operando), .b(4'b0010), .out(multiplier_1_out));  // open: cin, cout
  Subtractor #(.width(4)) subtractor_1 (.a(RgIN), .b(Operando), .out(subtractor_1_out));  // open: bin, bout
  Divider #(.width(4)) divider_1 (.a(Operando), .b(4'b0010), .out(divider_1_out));  // open: upper, rem
  Multiplexer #(.select(2), .width(4), .enable("false")) multiplexer_1 (
    .in0(adder_1_out), .in1(multiplier_1_out), .in2(subtractor_1_out), .in3(divider_1_out), .out(RgTO),
    .sel(ULA));
endmodule

module Reg4 (
  input  Clock,
  input  Load,
  input  [3:0] D,
  input  Clear,
  output [3:0] Q
);

  wire multiplexer_1_out, multiplexer_2_out, multiplexer_3_out, multiplexer_4_out;

  Multiplexer #(.enable("false")) multiplexer_1 (.in0(Q[3]), .in1(D[3]), .out(multiplexer_1_out), .sel(Load));
  D_Flip_Flop d_ff_1 (.clk(Clock), .D(multiplexer_1_out), .Q(Q[3]), .reset(Clear));  // open: Qn, preset
  Multiplexer #(.enable("false")) multiplexer_2 (.in0(Q[2]), .in1(D[2]), .out(multiplexer_2_out), .sel(Load));
  D_Flip_Flop d_ff_2 (.clk(Clock), .D(multiplexer_2_out), .Q(Q[2]), .reset(Clear));  // open: Qn, preset
  Multiplexer #(.enable("false")) multiplexer_3 (.in0(Q[1]), .in1(D[1]), .out(multiplexer_3_out), .sel(Load));
  D_Flip_Flop d_ff_3 (.clk(Clock), .D(multiplexer_3_out), .Q(Q[1]), .reset(Clear));  // open: Qn, preset
  Multiplexer #(.enable("false")) multiplexer_4 (.in0(Q[0]), .in1(D[0]), .out(multiplexer_4_out), .sel(Load));
  D_Flip_Flop d_ff_4 (.clk(Clock), .D(multiplexer_4_out), .Q(Q[0]), .reset(Clear));  // open: Qn, preset
endmodule

module Count8 (
  input  [3:0] Addr,
  input  Jump,
  input  Clock,
  input  Clear,
  output [7:0] Cont
);

  wire and_1_out, and_2_out, and_3_out, and_4_out, and_5_out, and_6_out, not_1_out;

  FF_T_JMP ff_t_jmp_1 (.Addr(Addr[0]), .Jump(Jump), .Clock(Clock), .T(1'b1), .Clear(not_1_out), .Q(Cont[0]));
  not not_1 (not_1_out, Clear);
  FF_T_JMP ff_t_jmp_2 (.Addr(Addr[1]), .Jump(Jump), .Clock(Clock), .T(Cont[0]), .Clear(not_1_out), .Q(Cont[1]));
  and and_1 (and_1_out, Cont[1], Cont[0]);
  FF_T_JMP ff_t_jmp_3 (.Addr(Addr[2]), .Jump(Jump), .Clock(Clock), .T(and_1_out), .Clear(not_1_out), .Q(Cont[2]));
  and and_2 (and_2_out, Cont[2], and_1_out);
  FF_T_JMP ff_t_jmp_4 (.Addr(Addr[3]), .Jump(Jump), .Clock(Clock), .T(and_2_out), .Clear(not_1_out), .Q(Cont[3]));
  and and_3 (and_3_out, Cont[3], and_2_out);
  FF_T_JMP ff_t_jmp_5 (.Addr(1'b0), .Jump(Jump), .Clock(Clock), .T(and_3_out), .Clear(not_1_out), .Q(Cont[4]));
  and and_4 (and_4_out, Cont[4], and_3_out);
  FF_T_JMP ff_t_jmp_6 (.Addr(1'b0), .Jump(Jump), .Clock(Clock), .T(and_4_out), .Clear(not_1_out), .Q(Cont[5]));
  and and_5 (and_5_out, Cont[5], and_4_out);
  FF_T_JMP ff_t_jmp_7 (.Addr(1'b0), .Jump(Jump), .Clock(Clock), .Clear(not_1_out), .Q(Cont[6]));  // open: T
  and and_6 (and_6_out, Cont[6], and_5_out);
  FF_T_JMP ff_t_jmp_8 (.Addr(1'b0), .Jump(Jump), .Clock(Clock), .T(and_6_out), .Clear(not_1_out), .Q(Cont[7]));
endmodule

module FF_T_JMP (
  input  Addr,
  input  Jump,
  input  Clock,
  input  T,
  input  Clear,
  output Q
);

  wire and_1_out, nand_1_out, not_1_out, or_1_out;

  not not_1 (not_1_out, Jump);
  nand nand_1 (nand_1_out, Addr, Jump);
  or or_1 (or_1_out, Addr, not_1_out);
  and and_1 (and_1_out, or_1_out, Clear);
  T_Flip_Flop #(.NegatePresetClear("true")) t_ff_1 (
    .clk(Clock), .T(T), .Q(Q), .preset(nand_1_out), .reset(and_1_out));  // open: Qn
endmodule

module ROM_256x16_1 (
  input  [7:0] busAddr8,
  input  CLK,
  output [15:0] busData16
);

  wire not_1_out;
  wire [15:0] ROM_CPU_data;

  ROM #(.dataWidth(16), .Select("low")) ROM_CPU (.addr(busAddr8), .data(ROM_CPU_data));
  Register #(.width(16), .Select("low")) Reg16 (.D(ROM_CPU_data), .Q(busData16), .clk(not_1_out));  // open: en, clr
  not not_1 (not_1_out, CLK);

  // Notes on the sheet:
  //   contents of ROM_CPU (hex, n*v repeats v):
  //   6005 9101 6202 6304 c08 0 0 0 400 6001 9001 9002 6302 6102 9302 6200 6001 800
endmodule

module ROM_256x16_2 (
  input  [7:0] busAddr8,
  input  CLK,
  output [15:0] busData16
);

  wire not_1_out;
  wire [15:0] ROM_CPU_data;

  Register #(.width(16), .Select("low")) Reg16 (.D(ROM_CPU_data), .Q(busData16), .clk(not_1_out));  // open: en, clr
  ROM #(.dataWidth(16), .Select("low")) ROM_CPU (.addr(busAddr8), .data(ROM_CPU_data));
  not not_1 (not_1_out, CLK);

  // Notes on the sheet:
  //   contents of ROM_CPU (hex, n*v repeats v):
  //   6004 9102 6201 6305 9002 6002 9003 400 c0d 4*0 9002 6302 6101 9302 6200 6003 800
endmodule
